# Fritzing sketch Hardware_schematics (saved by Fritzing 1.0.1rc)
breadboards: 1

parts:
  Raspberry_Pi_4_4GB = Raspberry Pi 4B
  HC-SR04_Sensor = HC-SR04 Ultrasonic Distance Sensor
  Bateria_10000mAh = LIPO-1000mAh [package=lipo-1000]  # not connected
  Infrarrojos_1 = fc-51 [package=THT]
  Infrarrojos_2 = fc-51 [package=THT]
  LDR_1 = Photocell (LDR) [power=0.25W dark_resistance_@0.01lx=300kΩ light_resistance_@100lx=400Ω luminance=10lx package=THT]
  LDR_2 = Photocell (LDR) [power=0.25W dark_resistance_@0.01lx=300kΩ light_resistance_@100lx=400Ω luminance=10lx package=THT]
  LDR_3 = Photocell (LDR) [power=0.25W dark_resistance_@0.01lx=300kΩ light_resistance_@100lx=400Ω luminance=10lx package=THT]
  Step-Up = mini boost module
  Pila_1 = Battery Holders [package=battery-aa-kit]
  Pila_2 = Battery Holders [package=battery-aa-kit]
  Pila_3 = Battery Holders [package=battery-aa-kit]
  Pila_4 = Battery Holders [package=battery-aa-kit]
  Pila_5 = Battery Holders [package=battery-aa-kit]
  Pila_6 = Battery Holders [package=battery-aa-kit]
  Motor_reductora_48_1_+_Roda_-_2 = DC Motor [voltage_(max)=6V voltage_(min)=3V]
  Motor_reductora_48_1_+_Roda_-_1 = DC Motor [voltage_(max)=6V voltage_(min)=3V]
  Relay_1 = Keyes Relay [package=THT]
  Relay_2 = Keyes Relay [package=THT]
  Relay_3 = Keyes Relay [package=THT]
  HC-SR04_Sensor1 = HC-SR04 Ultrasonic Distance Sensor
  LDR_4 = Photocell (LDR) [power=0.25W dark_resistance_@0.01lx=300kΩ light_resistance_@100lx=400Ω luminance=10lx package=THT]
  Camera = Rasberry Pi NIOR Camera [chip_label=IC package="DIP (Dual Inline) [THT]"]  # not connected
  S1 = H-Bridge with L298N
  VALVE1 = Plastic Solenoid Valve
  VALVE2 = Plastic Solenoid Valve
  VALVE3 = Plastic Solenoid Valve
  U1 = LCD-16X2 [package=lcd-8x2]

nets:
  VCC: Raspberry_Pi_4_4GB.5V, HC-SR04_Sensor.VCC, Infrarrojos_1.pin3, Infrarrojos_2.pin3, Relay_1.power, Relay_2.power, Relay_3.power, HC-SR04_Sensor1.VCC, U1.K
  N1: Raspberry_Pi_4_4GB.GPIO3, HC-SR04_Sensor1.TRIG
  GND: Raspberry_Pi_4_4GB.GND, HC-SR04_Sensor.GND, Infrarrojos_1.pin2, Infrarrojos_2.pin1, Infrarrojos_2.pin2, LDR_1.pin_1, LDR_2.pin_1, Step-Up.Pin_3, Relay_1.ground, Relay_2.ground, Relay_3.ground, HC-SR04_Sensor1.GND, S1.GND, S1.IN1, VALVE1.no_name_yet#2, VALVE2.no_name_yet#2, VALVE3.no_name_yet#2, U1.DB7
  N2: Raspberry_Pi_4_4GB.GPIO4, HC-SR04_Sensor.TRIG
  N3: Raspberry_Pi_4_4GB.GPIO17, LDR_2.pin_0, LDR_3.pin_1
  N4: Raspberry_Pi_4_4GB.GPIO27, LDR_1.pin_0, LDR_4.pin_1
  N5: Raspberry_Pi_4_4GB.GPIO23, Relay_1.signal
  N6: Raspberry_Pi_4_4GB.GPIO24, Relay_2.signal
  N7: Raspberry_Pi_4_4GB.GPIO25, Relay_3.signal
  N8: Raspberry_Pi_4_4GB.GPIO7, U1.DB5
  N9: Raspberry_Pi_4_4GB.GPIO12, S1.ENA
  N10: Raspberry_Pi_4_4GB.GPIO16, S1.IN2
  N11: Raspberry_Pi_4_4GB.GPIO20, S1.IN3
  N12: HC-SR04_Sensor.ECHO, LDR_3.pin_0
  N13: Step-Up.Pin_1, Pila_1.-
  N14: Step-Up.Pin_2, Pila_6.+
  N15: Step-Up.Pin_4, Relay_1.C, Relay_2.C, Relay_3.C
  N16: Pila_1.+, Pila_2.-
  N17: Pila_2.+, Pila_3.-
  N18: Pila_3.+, Pila_4.-
  N19: Pila_4.+, Pila_5.-
  N20: Pila_5.+, Pila_6.-
  N21: Motor_reductora_48_1_+_Roda_-_2.pin_1, S1.M1-02
  N22: Motor_reductora_48_1_+_Roda_-_2.pin_2, S1.M1-01
  N23: Motor_reductora_48_1_+_Roda_-_1.pin_1, S1.M2-02
  N24: Motor_reductora_48_1_+_Roda_-_1.pin_2, S1.M2-01
  N25: Relay_1.NO, VALVE3.no_name_yet#1
  N26: Relay_2.NO, VALVE2.no_name_yet#1
  N27: Relay_3.NO, VALVE1.no_name_yet#1
  N28: HC-SR04_Sensor1.ECHO, LDR_4.pin_0

custom parts:
  mini boost module: mini boost module.
  Keyes Relay: The Keyes 5V relay module is suitable for SCM development, home appliance control. It uses a 5V~12V TIL control signal which can control DC / AC signal.
  Rasberry Pi NIOR Camera: Camera
  H-Bridge with L298N: h-bridge
